// Logisim project 16 bit CPU.circ as structural Verilog: 4 circuits, main circuit main
module main (
  input  [15:0] in_1,
  input  [15:0] in_2,
  input  Reset,
  output clock,
  output [15:0] out_5,
  output [15:0] out_6,
  output [7:0] Op_Code,
  output [15:0] out_8
);

  wire alu_1_skip_enable, clock_1_out, decoder_1_f_write, decoder_1_load_enable, decoder_1_w_write,
       pc_decoder_1_clock_2, pc_decoder_1_count, pc_decoder_1_load;
  wire [2:0] n4_bit_to_7_seg_encoder_1_p1;
  wire [3:0] decoder_1_bit_select, n4_bit_to_7_seg_encoder_1_p3;
  wire [4:0] decoder_1_out_17;
  wire [15:0] alu_1_out_5, alu_1_out_6, counter_1_q, decoder_1_out_11, decoder_1_out_12, decoder_1_out_15,
       decoder_1_out_16, decoder_1_out_19, decoder_1_out_20, pc_decoder_1_out_8, ram_1_data, register_1_q,
       register_2_q;

  Clock clock_1 (.out(clock_1_out));
  PC_Decoder pc_decoder_1 (
    .in_1(decoder_1_load_enable), .in_5(decoder_1_out_20), .Skip_enable(alu_1_skip_enable),
    .in_6(counter_1_q), .clock(clock_1_out), .in_4(Reset), .Load(pc_decoder_1_load),
    .out_8(pc_decoder_1_out_8), .Count(pc_decoder_1_count), .clock_2(pc_decoder_1_clock_2));
  Counter #(.width(16), .max('hffff)) counter_1 (
    .load(pc_decoder_1_load), .D(pc_decoder_1_out_8), .count(pc_decoder_1_count), .Q(counter_1_q),
    .clk(pc_decoder_1_clock_2));  // open: carry, clr
  ROM #(.addrWidth(16), .dataWidth(24)) rom_1 (.addr(counter_1_q), .data({Op_Code, out_8}));  // open: sel
  Decoder decoder_1 (
    .in_2(register_1_q), .in_3(ram_1_data), .in_4(out_8), .in_5(alu_1_out_5), .Clock(clock_1_out),
    .in_7(in_1), .in_8(in_2), .Reset(Reset), .in_10(register_2_q), .Op_Code(Op_Code),
    .out_11(decoder_1_out_11), .out_12(decoder_1_out_12), .F_Write(decoder_1_f_write),
    .W_Write(decoder_1_w_write), .out_15(decoder_1_out_15), .out_16(decoder_1_out_16),
    .out_17(decoder_1_out_17), .Bit_Select(decoder_1_bit_select), .out_19(decoder_1_out_19),
    .out_20(decoder_1_out_20), .Load_enable(decoder_1_load_enable), .out_22(out_5), .out_23(out_6),
    .clk(clock));
  ALU alu_1 (
    .in_3(decoder_1_out_11), .in_4(decoder_1_out_12), .op_code(decoder_1_out_17),
    .bit_select(decoder_1_bit_select), .out_5(alu_1_out_5), .out_6(alu_1_out_6),
    .Skip_enable(alu_1_skip_enable));
  Register #(.width(16)) register_1 (
    .D(decoder_1_out_16), .Q(register_1_q), .clk(decoder_1_w_write), .clr(Reset));  // open: en
  Register #(.width(16), .trigger("falling")) register_2 (
    .D(alu_1_out_6), .Q(register_2_q), .clk(clock_1_out), .clr(Reset));  // open: en
  _7_Segment_Display #(.active("false")) u_7_segment_display_1 (
    .g(n4_bit_to_7_seg_encoder_1_p3[0]), .f(n4_bit_to_7_seg_encoder_1_p3[1]),
    .a(n4_bit_to_7_seg_encoder_1_p3[2]), .b(n4_bit_to_7_seg_encoder_1_p3[3]),
    .e(n4_bit_to_7_seg_encoder_1_p1[2]), .d(n4_bit_to_7_seg_encoder_1_p1[1]),
    .c(n4_bit_to_7_seg_encoder_1_p1[0]));  // open: dp
  // _4_bit_to_7_seg_encoder 4_bit_to_7_seg_encoder_1: pin names not known; wires that end beside it: n4_bit_to_7_seg_encoder_1_p1, out_5[3:0], n4_bit_to_7_seg_encoder_1_p3
  RAM #(.addrWidth(16), .dataWidth(16), .bus("separate")) ram_1 (
    .addr(decoder_1_out_19), .din(decoder_1_out_15), .data(ram_1_data), .clk(decoder_1_f_write), .clr(Reset));  // open: str, sel, ld

  // Notes on the sheet:
  //   Clk
  //   PC decoder
  //   PC
  //   Program Memory
  //   contents of rom_1 (hex, n*v repeats v):
  //   1e0000 1f0000 c0000 1c0000 1e0009 20000 e0ffff 210002 210000
  //   Literal
  //   Decoder
  //   ALU
  //   Status Register
  //   Input 1
  //   W Register
  //   Input 2
  //   Output 1
  //   F Register
  //   Output 2
endmodule

module Decoder (
  input  [7:0] Op_Code,
  input  [15:0] in_2,
  input  [15:0] in_3,
  input  [15:0] in_4,
  input  [15:0] in_5,
  input  Clock,
  input  [15:0] in_7,
  input  [15:0] in_8,
  input  Reset,
  input  [15:0] in_10,
  output [15:0] out_11,
  output [15:0] out_12,
  output F_Write,
  output W_Write,
  output [15:0] out_15,
  output [15:0] out_16,
  output [4:0] out_17,
  output [3:0] Bit_Select,
  output [15:0] out_19,
  output [15:0] out_20,
  output Load_enable,
  output [15:0] out_22,
  output [15:0] out_23,
  output clk
);

  wire and_13_out, and_26_out, and_28_out, and_29_out, and_31_out, and_32_out, and_33_out, and_34_out,
       and_35_out, buffer_1_out, buffer_2_out, buffer_3_out, buffer_4_out, buffer_5_out, d_ff_1_q, d_ff_1_qn,
       not_1_out, or_7_out, or_9_out, or_10_out, or_11_out, or_14_out, or_15_out, or_20_out, or_21_out,
       or_22_out, or_23_out, or_24_out, or_25_out, or_26_out, or_27_out, or_28_out;
  wire [0:0] and_21_out;
  wire [7:0] ROL_F_out;
  wire [8:0] XOR_WL_out;
  wire [8:1] MOD_WF_2_out, MUL_WF_2_out, XOR_WF_2_out;
  wire [15:0] and_2_out, and_3_out, and_4_out, and_5_out, and_6_out, and_7_out, and_8_out, and_10_out,
       and_11_out, and_12_out, and_15_out, and_16_out, and_17_out, and_18_out, and_19_out, and_20_out,
       and_22_out, and_23_out, and_25_out, and_30_out, or_13_out, or_16_out, or_17_out;
  wire [15:15] and_1_out, and_24_out, MOV_FW_out, MOV_LF_out, MOV_LW_out, MOV_WF_out, or_1_out, or_2_out,
       or_3_out, or_4_out, or_6_out, or_8_out, RIN_F_2_out, RIN_F_out, WOUT_F_2_out, WOUT_F_out,
       WOUT_L_2_out, WOUT_L_out;

  and and_1 (and_1_out[15], in_4[15], in_4[14], in_4[13], in_4[12], in_4[11], in_4[10], in_4[9], in_4[8], in_4[7], in_4[6], in_4[5], in_4[4], in_4[3], in_4[2], in_4[1], in_4[0]);
  and ADD_WF (MUL_WF_2_out[8], ~Op_Code[7], ~Op_Code[6], ~Op_Code[5], ~Op_Code[4], ~Op_Code[3], ~Op_Code[2], ~Op_Code[1], Op_Code[0]);  // AND_Gate
  assign and_2_out = {16{and_1_out[15]}} & in_10;  // AND_Gate and_2, 16 bits wide
  and ROL_F (ROL_F_out[0], ~Op_Code[7], ~Op_Code[6], ~Op_Code[5], Op_Code[4], Op_Code[3], ~Op_Code[2], Op_Code[1], ~Op_Code[0]);  // AND_Gate
  and MOV_LW (MOV_LW_out[15], ~Op_Code[7], ~Op_Code[6], ~Op_Code[5], Op_Code[4], Op_Code[3], Op_Code[2], Op_Code[1], ~Op_Code[0]);  // AND_Gate
  and ADD_WF_2 (MUL_WF_2_out[7], Op_Code[7], ~Op_Code[6], ~Op_Code[5], ~Op_Code[4], ~Op_Code[3], ~Op_Code[2], ~Op_Code[1], Op_Code[0]);  // AND_Gate
  or or_1 (or_1_out[15], MUL_WF_2_out[8], MUL_WF_2_out[7], XOR_WL_out[8], MUL_WF_2_out[5], MUL_WF_2_out[4], XOR_WL_out[7], MUL_WF_2_out[2], MUL_WF_2_out[1], XOR_WL_out[6], MOD_WF_2_out[8], MOD_WF_2_out[7], XOR_WL_out[5], MOD_WF_2_out[5], MOD_WF_2_out[4], XOR_WL_out[4], MOD_WF_2_out[2], MOD_WF_2_out[1], XOR_WL_out[3], XOR_WF_2_out[8], XOR_WF_2_out[7], XOR_WL_out[2], XOR_WF_2_out[5], XOR_WF_2_out[4], XOR_WL_out[1], XOR_WF_2_out[2], XOR_WF_2_out[1], XOR_WL_out[0]);
  and ROR_F (ROL_F_out[1], ~Op_Code[7], ~Op_Code[6], ~Op_Code[5], Op_Code[4], Op_Code[3], ~Op_Code[2], Op_Code[1], Op_Code[0]);  // AND_Gate
  and MOV_WF (MOV_WF_out[15], ~Op_Code[7], ~Op_Code[6], ~Op_Code[5], Op_Code[4], Op_Code[3], Op_Code[2], Op_Code[1], Op_Code[0]);  // AND_Gate
  assign and_3_out = {16{MOV_LW_out[15]}} & in_4;  // AND_Gate and_3, 16 bits wide
  and ADD_WL (XOR_WL_out[8], ~Op_Code[7], ~Op_Code[6], ~Op_Code[5], Op_Code[4], ~Op_Code[3], ~Op_Code[2], ~Op_Code[1], Op_Code[0]);  // AND_Gate
  assign and_4_out = {16{or_1_out[15]}} & in_2;  // AND_Gate and_4, 16 bits wide
  assign and_5_out = {16{or_3_out[15]}} & in_3;  // AND_Gate and_5, 16 bits wide
  assign and_6_out = {16{or_4_out[15]}} & in_4;  // AND_Gate and_6, 16 bits wide
  D_Flip_Flop d_ff_1 (.clk(Clock), .D(d_ff_1_qn), .Q(d_ff_1_q), .Qn(d_ff_1_qn), .reset(Reset));  // open: preset, en
  assign and_7_out = {16{MOV_WF_out[15]}} & in_2;  // AND_Gate and_7, 16 bits wide
  assign and_8_out = {16{MOV_FW_out[15]}} & in_3;  // AND_Gate and_8, 16 bits wide
  and and_9 (clk, and_13_out, in_4[15]);
  buf buffer_1 (buffer_1_out, buffer_2_out);
  buf buffer_2 (buffer_2_out, Clock);
  buf buffer_3 (buffer_3_out, buffer_1_out);
  and INCR_F (ROL_F_out[2], ~Op_Code[7], ~Op_Code[6], ~Op_Code[5], Op_Code[4], Op_Code[3], Op_Code[2], ~Op_Code[1], ~Op_Code[0]);  // AND_Gate
  and MOV_FW (MOV_FW_out[15], ~Op_Code[7], ~Op_Code[6], Op_Code[5], ~Op_Code[4], ~Op_Code[3], ~Op_Code[2], ~Op_Code[1], ~Op_Code[0]);  // AND_Gate
  assign and_10_out = {16{MOV_LF_out[15]}} & in_4;  // AND_Gate and_10, 16 bits wide
  or or_2 (or_2_out[15], MOV_FW_out[15], MOV_WF_out[15]);
  assign and_11_out = {16{or_2_out[15]}} & in_4;  // AND_Gate and_11, 16 bits wide
  and SUB_WF (MUL_WF_2_out[5], ~Op_Code[7], ~Op_Code[6], ~Op_Code[5], ~Op_Code[4], ~Op_Code[3], ~Op_Code[2], Op_Code[1], ~Op_Code[0]);  // AND_Gate
  buf buffer_4 (buffer_4_out, buffer_5_out);
  buf buffer_5 (buffer_5_out, buffer_3_out);
  and DECR_F (ROL_F_out[3], ~Op_Code[7], ~Op_Code[6], ~Op_Code[5], Op_Code[4], Op_Code[3], Op_Code[2], ~Op_Code[1], Op_Code[0]);  // AND_Gate
  and MOV_LF (MOV_LF_out[15], ~Op_Code[7], ~Op_Code[6], Op_Code[5], ~Op_Code[4], ~Op_Code[3], ~Op_Code[2], Op_Code[1], ~Op_Code[0]);  // AND_Gate
  assign and_12_out = {16{MOV_LF_out[15]}} & in_2;  // AND_Gate and_12, 16 bits wide
  and SUB_WF_2 (MUL_WF_2_out[4], Op_Code[7], ~Op_Code[6], ~Op_Code[5], ~Op_Code[4], ~Op_Code[3], ~Op_Code[2], Op_Code[1], ~Op_Code[0]);  // AND_Gate
  or or_3 (or_3_out[15], MUL_WF_2_out[8], MUL_WF_2_out[7], MUL_WF_2_out[5], MUL_WF_2_out[4], MUL_WF_2_out[2], MUL_WF_2_out[1], MOD_WF_2_out[8], MOD_WF_2_out[7], MOD_WF_2_out[5], MOD_WF_2_out[4], MOD_WF_2_out[2], MOD_WF_2_out[1], XOR_WF_2_out[8], XOR_WF_2_out[7], XOR_WF_2_out[5], XOR_WF_2_out[4], XOR_WF_2_out[2], XOR_WF_2_out[1]);
  and and_13 (and_13_out, ~d_ff_1_q, buffer_4_out);  // AND_Gate
  and BTSC_F (ROL_F_out[4], Op_Code[7], Op_Code[6], Op_Code[5], Op_Code[4]);
  and GOTO_L (Load_enable, ~Op_Code[7], ~Op_Code[6], Op_Code[5], ~Op_Code[4], ~Op_Code[3], ~Op_Code[2], ~Op_Code[1], Op_Code[0]);  // AND_Gate
  assign out_20 = {16{Load_enable}} & in_4;  // AND_Gate and_14, 16 bits wide
  and SUB_WL (XOR_WL_out[7], ~Op_Code[7], ~Op_Code[6], ~Op_Code[5], Op_Code[4], ~Op_Code[3], ~Op_Code[2], Op_Code[1], ~Op_Code[0]);  // AND_Gate
  and BTSS_F (ROL_F_out[5], Op_Code[7], Op_Code[6], Op_Code[5], ~Op_Code[4]);  // AND_Gate
  assign and_15_out = {16{RIN_F_out[15]}} & in_7;  // AND_Gate and_15, 16 bits wide
  assign and_16_out = {16{RIN_F_2_out[15]}} & in_8;  // AND_Gate and_16, 16 bits wide
  or or_4 (or_4_out[15], XOR_WL_out[8], XOR_WL_out[7], XOR_WL_out[6], XOR_WL_out[5], XOR_WL_out[4], XOR_WL_out[3], XOR_WL_out[2], XOR_WL_out[1], XOR_WL_out[0]);
  and BS_F (ROL_F_out[6], Op_Code[7], Op_Code[6], ~Op_Code[5], Op_Code[4]);  // AND_Gate
  and RIN_F (RIN_F_out[15], ~Op_Code[7], ~Op_Code[6], ~Op_Code[5], ~Op_Code[4], Op_Code[3], ~Op_Code[2], Op_Code[1], ~Op_Code[0]);  // AND_Gate
  and MUL_WF (MUL_WF_2_out[2], ~Op_Code[7], ~Op_Code[6], ~Op_Code[5], ~Op_Code[4], ~Op_Code[3], ~Op_Code[2], Op_Code[1], Op_Code[0]);  // AND_Gate
  and BC_F (ROL_F_out[7], Op_Code[7], Op_Code[6], ~Op_Code[5], ~Op_Code[4]);  // AND_Gate
  and RIN_F_2 (RIN_F_2_out[15], Op_Code[7], ~Op_Code[6], ~Op_Code[5], ~Op_Code[4], Op_Code[3], ~Op_Code[2], Op_Code[1], ~Op_Code[0]);  // AND_Gate
  and MUL_WF_2 (MUL_WF_2_out[1], Op_Code[7], ~Op_Code[6], ~Op_Code[5], ~Op_Code[4], ~Op_Code[3], ~Op_Code[2], Op_Code[1], Op_Code[0]);  // AND_Gate
  and WOUT_L (WOUT_L_out[15], ~Op_Code[7], ~Op_Code[6], ~Op_Code[5], ~Op_Code[4], Op_Code[3], ~Op_Code[2], Op_Code[1], Op_Code[0]);  // AND_Gate
  assign and_17_out = {16{WOUT_L_out[15]}} & in_4;  // AND_Gate and_17, 16 bits wide
  and MUL_WL (XOR_WL_out[6], ~Op_Code[7], ~Op_Code[6], ~Op_Code[5], Op_Code[4], ~Op_Code[3], ~Op_Code[2], Op_Code[1], Op_Code[0]);  // AND_Gate
  assign out_12 = and_5_out | and_6_out | {{15{1'b0}}, and_21_out[0]};  // OR_Gate or_5, 16 bits wide
  assign and_18_out = {16{WOUT_L_2_out[15]}} & in_4;  // AND_Gate and_18, 16 bits wide
  or or_6 (or_6_out[15], MUL_WF_2_out[8], XOR_WL_out[8], MUL_WF_2_out[5], XOR_WL_out[7], MUL_WF_2_out[2], XOR_WL_out[6], MOD_WF_2_out[8], XOR_WL_out[5], MOD_WF_2_out[5], XOR_WL_out[4], MOD_WF_2_out[2], XOR_WL_out[3], XOR_WF_2_out[8], XOR_WL_out[2], XOR_WF_2_out[5], XOR_WL_out[1], XOR_WF_2_out[2], XOR_WL_out[0]);
  and WOUT_L_2 (WOUT_L_2_out[15], Op_Code[7], ~Op_Code[6], ~Op_Code[5], ~Op_Code[4], Op_Code[3], ~Op_Code[2], Op_Code[1], Op_Code[0]);  // AND_Gate
  assign and_19_out = {16{WOUT_F_out[15]}} & in_3;  // AND_Gate and_19, 16 bits wide
  assign and_20_out = {16{WOUT_F_2_out[15]}} & in_3;  // AND_Gate and_20, 16 bits wide
  and MUH_WF (MOD_WF_2_out[8], ~Op_Code[7], ~Op_Code[6], ~Op_Code[5], ~Op_Code[4], ~Op_Code[3], Op_Code[2], ~Op_Code[1], ~Op_Code[0]);  // AND_Gate
  and and_21 (and_21_out[0], in_4[15], in_4[14], in_4[13], in_4[12], in_4[11], in_4[10], in_4[9], in_4[8], in_4[6], in_4[5], in_4[4], in_4[3], in_4[2], in_4[1], in_4[0], in_4[7]);
  not not_1 (not_1_out, and_21_out[0]);
  or or_7 (or_7_out, ROL_F_out[7], ROL_F_out[6], ROL_F_out[5], ROL_F_out[4], ROL_F_out[3], ROL_F_out[2], ROL_F_out[1], ROL_F_out[0]);
  and WOUT_F (WOUT_F_out[15], ~Op_Code[7], ~Op_Code[6], ~Op_Code[5], ~Op_Code[4], Op_Code[3], Op_Code[2], ~Op_Code[1], ~Op_Code[0]);  // AND_Gate
  and MUH_WF_2 (MOD_WF_2_out[7], Op_Code[7], ~Op_Code[6], ~Op_Code[5], ~Op_Code[4], ~Op_Code[3], Op_Code[2], ~Op_Code[1], ~Op_Code[0]);  // AND_Gate
  assign and_22_out = {16{or_8_out[15]}} & in_5;  // AND_Gate and_22, 16 bits wide
  assign and_23_out = {16{or_6_out[15]}} & in_5;  // AND_Gate and_23, 16 bits wide
  and and_24 (and_24_out[15], not_1_out, or_7_out);
  or or_8 (or_8_out[15], XOR_WF_2_out[1], XOR_WF_2_out[4], XOR_WF_2_out[7], MOD_WF_2_out[1], MOD_WF_2_out[4], MOD_WF_2_out[7], MUL_WF_2_out[1], MUL_WF_2_out[4], MUL_WF_2_out[7]);
  or or_9 (or_9_out, ROL_F_out[4], ROL_F_out[5]);
  assign and_25_out = {16{and_24_out[15]}} & in_3;  // AND_Gate and_25, 16 bits wide
  and WOUT_F_2 (WOUT_F_2_out[15], Op_Code[7], ~Op_Code[6], ~Op_Code[5], ~Op_Code[4], Op_Code[3], Op_Code[2], ~Op_Code[1], ~Op_Code[0]);  // AND_Gate
  and MUH_WL (XOR_WL_out[5], ~Op_Code[7], ~Op_Code[6], ~Op_Code[5], Op_Code[4], ~Op_Code[3], Op_Code[2], ~Op_Code[1], ~Op_Code[0]);  // AND_Gate
  and and_26 (and_26_out, ~or_9_out, and_24_out[15]);  // AND_Gate
  // AND_Gate and_27 is placed but not wired
  or or_10 (or_10_out, WOUT_L_out[15], WOUT_F_out[15]);
  or or_11 (or_11_out, WOUT_L_2_out[15], WOUT_F_2_out[15]);
  and DIV_WF (MOD_WF_2_out[5], ~Op_Code[7], ~Op_Code[6], ~Op_Code[5], ~Op_Code[4], ~Op_Code[3], Op_Code[2], ~Op_Code[1], Op_Code[0]);  // AND_Gate
  and and_28 (and_28_out, or_8_out[15], and_13_out);
  and and_29 (and_29_out, or_6_out[15], and_13_out);
  assign and_30_out = {16{and_24_out[15]}} & in_5;  // AND_Gate and_30, 16 bits wide
  and and_31 (and_31_out, or_10_out, and_13_out);
  and and_32 (and_32_out, or_11_out, and_13_out);
  and DIV_WF_2 (MOD_WF_2_out[4], Op_Code[7], ~Op_Code[6], ~Op_Code[5], ~Op_Code[4], ~Op_Code[3], Op_Code[2], ~Op_Code[1], Op_Code[0]);  // AND_Gate
  assign out_11 = and_4_out | and_25_out | and_2_out;  // OR_Gate or_12, 16 bits wide
  and and_33 (and_33_out, and_26_out, and_13_out);
  assign or_13_out = and_7_out | and_10_out | and_15_out | and_16_out;  // OR_Gate or_13, 16 bits wide
  or or_14 (or_14_out, MOV_LW_out[15], MOV_FW_out[15]);
  or or_15 (or_15_out, MOV_WF_out[15], MOV_LF_out[15], RIN_F_out[15], RIN_F_2_out[15]);
  and DIV_WL (XOR_WL_out[4], ~Op_Code[7], ~Op_Code[6], ~Op_Code[5], Op_Code[4], ~Op_Code[3], Op_Code[2], ~Op_Code[1], Op_Code[0]);  // AND_Gate
  and and_34 (and_34_out, or_15_out, and_13_out);
  and and_35 (and_35_out, or_14_out, and_13_out);
  assign or_16_out = and_17_out | and_19_out;  // OR_Gate or_16, 16 bits wide
  assign or_17_out = and_18_out | and_20_out;  // OR_Gate or_17, 16 bits wide
  and MOD_WF (MOD_WF_2_out[2], ~Op_Code[7], ~Op_Code[6], ~Op_Code[5], ~Op_Code[4], ~Op_Code[3], Op_Code[2], Op_Code[1], ~Op_Code[0]);  // AND_Gate
  assign Bit_Select = Op_Code[3:0] | Op_Code[3:0] | Op_Code[3:0] | Op_Code[3:0];  // OR_Gate or_18, 4 bits wide
  Register #(.width(16)) register_1 (.D(or_16_out), .Q(out_22), .clk(and_31_out), .clr(Reset));  // open: en
  Register #(.width(16)) register_2 (.D(or_17_out), .Q(out_23), .clk(and_32_out), .clr(Reset));  // open: en
  and MOD_WF_2 (MOD_WF_2_out[1], Op_Code[7], ~Op_Code[6], ~Op_Code[5], ~Op_Code[4], ~Op_Code[3], Op_Code[2], Op_Code[1], ~Op_Code[0]);  // AND_Gate
  assign out_19 = and_11_out | and_12_out;  // OR_Gate or_19, 16 bits wide
  and MOD_WL (XOR_WL_out[3], ~Op_Code[7], ~Op_Code[6], ~Op_Code[5], Op_Code[4], ~Op_Code[3], Op_Code[2], Op_Code[1], ~Op_Code[0]);  // AND_Gate
  or or_20 (or_20_out, XOR_WL_out[8], MUL_WF_2_out[7], MUL_WF_2_out[8]);
  or or_21 (or_21_out, XOR_WL_out[7], MUL_WF_2_out[4], MUL_WF_2_out[5]);
  or or_22 (or_22_out, XOR_WL_out[6], MUL_WF_2_out[1], MUL_WF_2_out[2]);
  or or_23 (or_23_out, XOR_WL_out[5], MOD_WF_2_out[7], MOD_WF_2_out[8]);
  or or_24 (or_24_out, XOR_WL_out[4], MOD_WF_2_out[4], MOD_WF_2_out[5]);
  or or_25 (or_25_out, XOR_WL_out[3], MOD_WF_2_out[1], MOD_WF_2_out[2]);
  or or_26 (or_26_out, XOR_WL_out[2], XOR_WF_2_out[7], XOR_WF_2_out[8]);
  or or_27 (or_27_out, XOR_WL_out[1], XOR_WF_2_out[4], XOR_WF_2_out[5]);
  or or_28 (or_28_out, XOR_WL_out[0], XOR_WF_2_out[1], XOR_WF_2_out[2]);
  and NAND_WF (XOR_WF_2_out[8], ~Op_Code[7], ~Op_Code[6], ~Op_Code[5], ~Op_Code[4], ~Op_Code[3], Op_Code[2], Op_Code[1], Op_Code[0]);  // AND_Gate
  or or_29 (F_Write, and_28_out, and_33_out, and_34_out);
  and NAND_WF_2 (XOR_WF_2_out[7], Op_Code[7], ~Op_Code[6], ~Op_Code[5], ~Op_Code[4], ~Op_Code[3], Op_Code[2], Op_Code[1], Op_Code[0]);  // AND_Gate
  or or_30 (W_Write, and_29_out, and_35_out);
  assign out_15 = and_22_out | and_30_out | or_13_out;  // OR_Gate or_31, 16 bits wide
  assign out_16 = and_23_out | and_3_out | and_8_out;  // OR_Gate or_32, 16 bits wide
  and NAND_WL (XOR_WL_out[2], ~Op_Code[7], ~Op_Code[6], ~Op_Code[5], Op_Code[4], ~Op_Code[3], Op_Code[2], Op_Code[1], Op_Code[0]);  // AND_Gate
  Priority_Encoder #(.select(5)) priority_encoder_1 (
    .in0(1'b1), .in1(or_20_out), .in2(or_21_out), .in3(or_22_out), .in4(or_23_out), .in5(or_24_out),
    .in6(or_25_out), .in7(or_26_out), .in8(or_27_out), .in9(or_28_out), .in10(ROL_F_out[0]),
    .in11(ROL_F_out[1]), .in12(ROL_F_out[2]), .in13(ROL_F_out[3]), .in14(ROL_F_out[4]), .in15(ROL_F_out[5]),
    .in16(ROL_F_out[6]), .in17(ROL_F_out[7]), .out(out_17));  // open: in18, in19, in20, in21, in22, in23, in24, in25, in26, in27, in28, in29, in30, in31, gs, en_out, en_in
  and NOR_WF (XOR_WF_2_out[5], ~Op_Code[7], ~Op_Code[6], ~Op_Code[5], ~Op_Code[4], Op_Code[3], ~Op_Code[2], ~Op_Code[1], ~Op_Code[0]);  // AND_Gate
  and NOR_WF_2 (XOR_WF_2_out[4], Op_Code[7], ~Op_Code[6], ~Op_Code[5], ~Op_Code[4], Op_Code[3], ~Op_Code[2], ~Op_Code[1], ~Op_Code[0]);  // AND_Gate
  and NOR_WL (XOR_WL_out[1], ~Op_Code[7], ~Op_Code[6], ~Op_Code[5], Op_Code[4], Op_Code[3], ~Op_Code[2], ~Op_Code[1], ~Op_Code[0]);  // AND_Gate
  and XOR_WF (XOR_WF_2_out[2], ~Op_Code[7], ~Op_Code[6], ~Op_Code[5], ~Op_Code[4], Op_Code[3], ~Op_Code[2], ~Op_Code[1], Op_Code[0]);  // AND_Gate
  and XOR_WF_2 (XOR_WF_2_out[1], Op_Code[7], ~Op_Code[6], ~Op_Code[5], ~Op_Code[4], Op_Code[3], ~Op_Code[2], ~Op_Code[1], Op_Code[0]);  // AND_Gate
  and XOR_WL (XOR_WL_out[0], ~Op_Code[7], ~Op_Code[6], ~Op_Code[5], Op_Code[4], Op_Code[3], ~Op_Code[2], ~Op_Code[1], Op_Code[0]);  // AND_Gate

  // Notes on the sheet:
  //   W
  //   F
  //   Literal
  //   ALU Output
  //   Input 1
  //   Input 2
  //   Status Register
  //   ALU A
  //   ALU B
  //   F address
  //   Load counter
  //   Output 1
  //   Output 2
  //   F
  //   W
  //   ALU Op codes
endmodule

module ALU (
  input  [4:0] op_code,
  input  [3:0] bit_select,
  input  [15:0] in_3,
  input  [15:0] in_4,
  output [15:0] out_5,
  output [15:0] out_6,
  output Skip_enable
);

  wire adder_1_cout, and_1_out, and_2_out, and_3_out, and_4_out, and_5_out, and_6_out, and_7_out, and_8_out,
       and_9_out, and_10_out, and_11_out, and_12_out, and_13_out, and_14_out, and_15_out, and_16_out,
       and_17_out, and_18_out, and_19_out, and_20_out, and_21_out, and_22_out, and_23_out, and_24_out,
       and_25_out, and_26_out, and_27_out, and_28_out, and_29_out, and_30_out, and_31_out, and_32_out,
       and_33_out, and_34_out, and_35_out, and_36_out, and_37_out, and_38_out, and_39_out, and_40_out,
       and_41_out, and_42_out, and_43_out, and_44_out, and_45_out, and_46_out, and_47_out, and_48_out,
       and_49_out, and_50_out, and_51_out, and_52_out, and_53_out, and_54_out, and_55_out, and_56_out,
       and_57_out, and_58_out, and_59_out, and_60_out, and_61_out, and_62_out, and_63_out, and_64_out,
       and_65_out, and_66_out, and_68_out, and_69_out, decoder_1_out0, decoder_1_out1, decoder_1_out2,
       decoder_1_out3, decoder_1_out4, decoder_1_out5, decoder_1_out6, decoder_1_out7, decoder_1_out8,
       decoder_1_out9, decoder_1_out10, decoder_1_out11, decoder_1_out12, decoder_1_out13, decoder_1_out14,
       decoder_1_out15, decoder_2_out0, decoder_2_out1, decoder_2_out2, decoder_2_out3, decoder_2_out4,
       decoder_2_out5, decoder_2_out6, decoder_2_out7, decoder_2_out8, decoder_2_out9, decoder_2_out10,
       decoder_2_out11, decoder_2_out12, decoder_2_out13, decoder_2_out14, decoder_2_out15,
       multiplexer_1_out, or_33_out, or_34_out, subtractor_1_bout;
  wire [15:0] adder_1_out, adder_2_out, divider_1_out, divider_1_rem, multiplier_1_cout, multiplier_1_out,
       nand_1_out, nor_1_out, or_1_out, or_17_out, shifter_1_out, shifter_2_out, subtractor_1_out,
       subtractor_2_out, xor_1_out;
  wire [15:15] multiplexer_2_out, not_1_out;

  Decoder_part #(.select(4), .enable("false")) decoder_1 (
    .out0(decoder_1_out0), .out1(decoder_1_out1), .out2(decoder_1_out2), .out3(decoder_1_out3),
    .out4(decoder_1_out4), .out5(decoder_1_out5), .out6(decoder_1_out6), .out7(decoder_1_out7),
    .out8(decoder_1_out8), .out9(decoder_1_out9), .out10(decoder_1_out10), .out11(decoder_1_out11),
    .out12(decoder_1_out12), .out13(decoder_1_out13), .out14(decoder_1_out14), .out15(decoder_1_out15),
    .sel(bit_select));
  Decoder_part #(.select(4), .enable("false")) decoder_2 (
    .out0(decoder_2_out0), .out1(decoder_2_out1), .out2(decoder_2_out2), .out3(decoder_2_out3),
    .out4(decoder_2_out4), .out5(decoder_2_out5), .out6(decoder_2_out6), .out7(decoder_2_out7),
    .out8(decoder_2_out8), .out9(decoder_2_out9), .out10(decoder_2_out10), .out11(decoder_2_out11),
    .out12(decoder_2_out12), .out13(decoder_2_out13), .out14(decoder_2_out14), .out15(decoder_2_out15),
    .sel(bit_select));
  and and_1 (and_1_out, ~decoder_1_out0, in_3[0]);  // AND_Gate
  and and_2 (and_2_out, decoder_1_out0, 1'b1);
  and and_3 (and_3_out, ~decoder_1_out1, in_3[1]);  // AND_Gate
  and and_4 (and_4_out, decoder_1_out1, 1'b1);
  and and_5 (and_5_out, ~decoder_1_out2, in_3[2]);  // AND_Gate
  and and_6 (and_6_out, decoder_1_out2, 1'b1);
  and and_7 (and_7_out, ~decoder_1_out3, in_3[3]);  // AND_Gate
  and and_8 (and_8_out, decoder_1_out3, 1'b1);
  and and_9 (and_9_out, ~decoder_1_out4, in_3[4]);  // AND_Gate
  and and_10 (and_10_out, decoder_1_out4, 1'b1);
  and and_11 (and_11_out, ~decoder_1_out5, in_3[5]);  // AND_Gate
  and and_12 (and_12_out, decoder_1_out5, 1'b1);
  and and_13 (and_13_out, ~decoder_1_out6, in_3[6]);  // AND_Gate
  and and_14 (and_14_out, decoder_1_out6, 1'b1);
  and and_15 (and_15_out, ~decoder_1_out7, in_3[7]);  // AND_Gate
  and and_16 (and_16_out, decoder_1_out7, 1'b1);
  and and_17 (and_17_out, ~decoder_1_out8, in_3[8]);  // AND_Gate
  and and_18 (and_18_out, decoder_1_out8, 1'b1);
  and and_19 (and_19_out, ~decoder_1_out9, in_3[9]);  // AND_Gate
  and and_20 (and_20_out, decoder_1_out9, 1'b1);
  and and_21 (and_21_out, ~decoder_1_out10, in_3[10]);  // AND_Gate
  and and_22 (and_22_out, decoder_1_out10, 1'b1);
  and and_23 (and_23_out, ~decoder_1_out11, in_3[11]);  // AND_Gate
  and and_24 (and_24_out, decoder_1_out11, 1'b1);
  and and_25 (and_25_out, ~decoder_1_out12, in_3[12]);  // AND_Gate
  and and_26 (and_26_out, decoder_1_out12, 1'b1);
  and and_27 (and_27_out, ~decoder_1_out13, in_3[13]);  // AND_Gate
  and and_28 (and_28_out, decoder_1_out13, 1'b1);
  and and_29 (and_29_out, ~decoder_1_out14, in_3[14]);  // AND_Gate
  and and_30 (and_30_out, decoder_1_out14, 1'b1);
  and and_31 (and_31_out, ~decoder_1_out15, in_3[15]);  // AND_Gate
  and and_32 (and_32_out, decoder_1_out15, 1'b1);
  and and_33 (and_33_out, ~decoder_2_out0, in_3[0]);  // AND_Gate
  and and_34 (and_34_out, decoder_2_out0, 1'b0);
  and and_35 (and_35_out, ~decoder_2_out1, in_3[1]);  // AND_Gate
  and and_36 (and_36_out, decoder_2_out1, 1'b0);
  and and_37 (and_37_out, ~decoder_2_out2, in_3[2]);  // AND_Gate
  and and_38 (and_38_out, decoder_2_out2, 1'b0);
  and and_39 (and_39_out, ~decoder_2_out3, in_3[3]);  // AND_Gate
  and and_40 (and_40_out, decoder_2_out3, 1'b0);
  and and_41 (and_41_out, ~decoder_2_out4, in_3[4]);  // AND_Gate
  and and_42 (and_42_out, decoder_2_out4, 1'b0);
  and and_43 (and_43_out, ~decoder_2_out5, in_3[5]);  // AND_Gate
  and and_44 (and_44_out, decoder_2_out5, 1'b0);
  and and_45 (and_45_out, ~decoder_2_out6, in_3[6]);  // AND_Gate
  and and_46 (and_46_out, decoder_2_out6, 1'b0);
  and and_47 (and_47_out, ~decoder_2_out7, in_3[7]);  // AND_Gate
  and and_48 (and_48_out, decoder_2_out7, 1'b0);
  and and_49 (and_49_out, ~decoder_2_out8, in_3[8]);  // AND_Gate
  and and_50 (and_50_out, decoder_2_out8, 1'b0);
  and and_51 (and_51_out, ~decoder_2_out9, in_3[9]);  // AND_Gate
  and and_52 (and_52_out, decoder_2_out9, 1'b0);
  and and_53 (and_53_out, ~decoder_2_out10, in_3[10]);  // AND_Gate
  and and_54 (and_54_out, decoder_2_out10, 1'b0);
  and and_55 (and_55_out, ~decoder_2_out11, in_3[11]);  // AND_Gate
  and and_56 (and_56_out, decoder_2_out11, 1'b0);
  and and_57 (and_57_out, ~decoder_2_out12, in_3[12]);  // AND_Gate
  and and_58 (and_58_out, decoder_2_out12, 1'b0);
  and and_59 (and_59_out, ~decoder_2_out13, in_3[13]);  // AND_Gate
  and and_60 (and_60_out, decoder_2_out13, 1'b0);
  and and_61 (and_61_out, ~decoder_2_out14, in_3[14]);  // AND_Gate
  and and_62 (and_62_out, decoder_2_out14, 1'b0);
  and and_63 (and_63_out, ~decoder_2_out15, in_3[15]);  // AND_Gate
  and and_64 (and_64_out, decoder_2_out15, 1'b0);
  Adder #(.width(16)) adder_1 (.a(in_3), .b(in_4), .out(adder_1_out), .cout(adder_1_cout));  // open: cin
  Subtractor #(.width(16)) subtractor_1 (
    .a(in_3), .b(in_4), .out(subtractor_1_out), .bout(subtractor_1_bout));  // open: bin
  Multiplier #(.width(16)) multiplier_1 (
    .a(in_3), .b(in_4), .out(multiplier_1_out), .cout(multiplier_1_cout));  // open: cin
  Divider #(.width(16)) divider_1 (.a(in_3), .b(in_4), .out(divider_1_out), .rem(divider_1_rem));  // open: upper
  assign nand_1_out = ~(in_3 & in_4);  // NAND_Gate nand_1, 16 bits wide
  assign nor_1_out = ~(in_3 | in_4);  // NOR_Gate nor_1, 16 bits wide
  assign xor_1_out = in_3 ^ in_4;  // XOR_Gate xor_1, 16 bits wide
  Shifter #(.width(16), .shift("rl")) shifter_1 (.in(in_3), .\dist (4'b0001), .out(shifter_1_out));
  Shifter #(.width(16), .shift("rr")) shifter_2 (.in(in_3), .\dist (4'b0001), .out(shifter_2_out));
  Adder #(.width(16)) adder_2 (.a(in_3), .b(16'h1), .out(adder_2_out));  // open: cin, cout
  Subtractor #(.width(16)) subtractor_2 (.a(in_3), .b(16'h1), .out(subtractor_2_out));  // open: bin, bout
  Multiplexer #(.select(4), .enable("false")) multiplexer_1 (
    .in0(in_3[0]), .in1(in_3[1]), .in2(in_3[2]), .in3(in_3[3]), .in4(in_3[4]), .in5(in_3[5]), .in6(in_3[6]),
    .in7(in_3[7]), .in8(in_3[8]), .in9(in_3[9]), .in10(in_3[10]), .in11(in_3[11]), .in12(in_3[12]),
    .in13(in_3[13]), .in14(in_3[14]), .in15(in_3[15]), .out(multiplexer_1_out), .sel(bit_select));
  Multiplexer #(.select(4), .enable("false")) multiplexer_2 (
    .in0(in_3[0]), .in1(in_3[1]), .in2(in_3[2]), .in3(in_3[3]), .in4(in_3[4]), .in5(in_3[5]), .in6(in_3[6]),
    .in7(in_3[7]), .in8(in_3[8]), .in9(in_3[9]), .in10(in_3[10]), .in11(in_3[11]), .in12(in_3[12]),
    .in13(in_3[13]), .in14(in_3[14]), .in15(in_3[15]), .out(multiplexer_2_out[15]), .sel(bit_select));
  not not_1 (not_1_out[15], multiplexer_1_out);
  or or_1 (or_1_out[0], and_1_out, and_2_out);
  or or_2 (or_1_out[1], and_3_out, and_4_out);
  or or_3 (or_1_out[2], and_5_out, and_6_out);
  or or_4 (or_1_out[3], and_7_out, and_8_out);
  or or_5 (or_1_out[4], and_9_out, and_10_out);
  or or_6 (or_1_out[5], and_11_out, and_12_out);
  or or_7 (or_1_out[6], and_13_out, and_14_out);
  or or_8 (or_1_out[7], and_15_out, and_16_out);
  or or_9 (or_1_out[8], and_17_out, and_18_out);
  or or_10 (or_1_out[9], and_19_out, and_20_out);
  or or_11 (or_1_out[10], and_21_out, and_22_out);
  or or_12 (or_1_out[11], and_23_out, and_24_out);
  or or_13 (or_1_out[12], and_25_out, and_26_out);
  or or_14 (or_1_out[13], and_27_out, and_28_out);
  or or_15 (or_1_out[14], and_29_out, and_30_out);
  or or_16 (or_1_out[15], and_31_out, and_32_out);
  or or_17 (or_17_out[0], and_33_out, and_34_out);
  or or_18 (or_17_out[1], and_35_out, and_36_out);
  or or_19 (or_17_out[2], and_37_out, and_38_out);
  or or_20 (or_17_out[3], and_39_out, and_40_out);
  or or_21 (or_17_out[4], and_41_out, and_42_out);
  or or_22 (or_17_out[5], and_43_out, and_44_out);
  or or_23 (or_17_out[6], and_45_out, and_46_out);
  or or_24 (or_17_out[7], and_47_out, and_48_out);
  or or_25 (or_17_out[8], and_49_out, and_50_out);
  or or_26 (or_17_out[9], and_51_out, and_52_out);
  or or_27 (or_17_out[10], and_53_out, and_54_out);
  or or_28 (or_17_out[11], and_55_out, and_56_out);
  or or_29 (or_17_out[12], and_57_out, and_58_out);
  or or_30 (or_17_out[13], and_59_out, and_60_out);
  or or_31 (or_17_out[14], and_61_out, and_62_out);
  or or_32 (or_17_out[15], and_63_out, and_64_out);
  and and_65 (and_65_out, op_code[4], ~op_code[3], ~op_code[2], ~op_code[1], ~op_code[0]);  // AND_Gate
  and and_66 (and_66_out, op_code[4], ~op_code[3], ~op_code[2], ~op_code[1], op_code[0]);  // AND_Gate
  or or_33 (or_33_out, and_65_out, and_66_out);
  Multiplexer #(.select(2), .enable("false")) multiplexer_3 (
    .in0(1'b0), .in1(adder_1_cout), .in2(subtractor_1_bout), .in3(1'b0), .out(out_6[2]), .sel(op_code[1:0]));
  Multiplexer #(.select(5), .width(16), .enable("false")) multiplexer_4 (
    .in0({16{1'b0}}), .in1(adder_1_out), .in2(subtractor_1_out), .in3(multiplier_1_out),
    .in4(multiplier_1_cout), .in5(divider_1_out), .in6(divider_1_rem), .in7(nand_1_out), .in8(nor_1_out),
    .in9(xor_1_out), .in10(shifter_1_out), .in11(shifter_2_out), .in12(adder_2_out), .in13(subtractor_2_out),
    .in14({16{not_1_out[15]}}), .in15({16{multiplexer_2_out[15]}}), .in16(or_1_out), .in17(or_17_out),
    .out(out_5), .sel(op_code));  // open: in18, in19, in20, in21, in22, in23, in24, in25, in26, in27, in28, in29, in30, in31
  and and_67 (out_6[15], out_5[15], or_33_out, in_4[0]);
  not not_2 (out_6[0], or_34_out);
  or or_34 (or_34_out, out_5[0], out_5[1], out_5[2], out_5[3], out_5[4], out_5[5], out_5[6], out_5[7], out_5[8], out_5[9], out_5[10], out_5[11], out_5[12], out_5[13], out_5[14], out_5[15]);
  xnor even_parity_1 (out_6[3], out_5[0], out_5[1], out_5[2], out_5[3], out_5[4], out_5[5], out_5[6], out_5[7], out_5[8], out_5[9], out_5[10], out_5[11], out_5[12], out_5[13], out_5[14], out_5[15]);
  and and_68 (and_68_out, out_5[15], not_1_out[15]);
  and and_69 (and_69_out, out_5[15], multiplexer_2_out[15]);
  or or_35 (Skip_enable, and_68_out, and_69_out);

  assign {out_6[14:4], out_6[1]} = {{11{1'b0}}, out_5[15]};

  // Notes on the sheet:
  //   Input A
  //   Input B
  //   Carry
  //   Zero
  //   Negative
  //   Parity
  //   Output
  //   Flags
endmodule

module PC_Decoder (
  input  in_1,
  input  Skip_enable,
  input  clock,
  input  in_4,
  input  [15:0] in_5,
  input  [15:0] in_6,
  output Load,
  output [15:0] out_8,
  output Count,
  output clock_2
);

  wire and_4_out, buffer_1_out, buffer_2_out, buffer_3_out, buffer_4_out, buffer_5_out, buffer_6_out,
       buffer_7_out, buffer_8_out, buffer_9_out, d_ff_1_q, d_ff_1_qn, or_3_out;
  wire [15:0] adder_1_out, and_1_out, and_2_out, and_3_out;

  assign and_1_out = {16{in_1}} & in_5;  // AND_Gate and_1, 16 bits wide
  assign and_2_out = {16{Skip_enable}} & adder_1_out;  // AND_Gate and_2, 16 bits wide
  Adder #(.width(16)) adder_1 (.a(in_6), .b(16'h2), .out(adder_1_out));  // open: cin, cout
  buf buffer_1 (buffer_1_out, in_4);
  assign and_3_out = {16{in_4}} & {16{1'b1}};  // AND_Gate and_3, 16 bits wide
  buf buffer_2 (buffer_2_out, buffer_4_out);
  buf buffer_3 (buffer_3_out, buffer_1_out);
  buf buffer_4 (buffer_4_out, buffer_3_out);
  D_Flip_Flop d_ff_1 (.clk(clock), .D(d_ff_1_qn), .Q(d_ff_1_q), .Qn(d_ff_1_qn), .reset(in_4));  // open: preset, en
  buf buffer_5 (buffer_5_out, buffer_6_out);
  buf buffer_6 (buffer_6_out, clock);
  buf buffer_7 (buffer_7_out, buffer_5_out);
  buf buffer_8 (buffer_8_out, buffer_7_out);
  buf buffer_9 (buffer_9_out, buffer_8_out);
  or or_1 (Load, Skip_enable, in_4, in_1);
  assign out_8 = and_1_out | and_3_out | and_2_out;  // OR_Gate or_2, 16 bits wide
  not not_1 (Count, or_3_out);
  or or_3 (or_3_out, in_1, in_4, Skip_enable);
  and and_4 (and_4_out, d_ff_1_q, buffer_9_out);
  or or_4 (clock_2, buffer_2_out, and_4_out);

  // Notes on the sheet:
  //   Goto enable
  //   Load Value
  //   Current Value
  //   reset
  //   Value
endmodule
